// Logisim project Verification_of_De-Morgan's_First_Law.circ as structural Verilog: 1 circuit, main circuit main
module main (
  input  A,
  input  A_2,
  input  B,
  input  B_2,
  input  A_3,
  input  A_4,
  input  B_3,
  input  B_4,
  output out_9,
  output out_10,
  output out_11,
  output out_12,
  output out_13,
  output out_14,
  output out_15,
  output out_16
);

  wire not_1_out, not_2_out, not_3_out, not_4_out, not_5_out, not_6_out, not_7_out, not_8_out;

  nand nand_1 (out_9, A, B);
  not not_1 (not_1_out, A);
  not not_2 (not_2_out, B);
  nand nand_2 (out_14, A_4, B_4);
  not not_3 (not_3_out, A_4);
  not not_4 (not_4_out, B_4);
  or or_1 (out_11, not_1_out, not_2_out);
  or or_2 (out_16, not_3_out, not_4_out);
  nand nand_3 (out_10, A_2, B_2);
  not not_5 (not_5_out, A_2);
  not not_6 (not_6_out, B_2);
  nand nand_4 (out_13, A_3, B_3);
  not not_7 (not_7_out, A_3);
  not not_8 (not_8_out, B_3);
  or or_3 (out_12, not_5_out, not_6_out);
  or or_4 (out_15, not_7_out, not_8_out);

  // Notes on the sheet:
  //   Fig 2.1.1 De-Morgan's First Law(0,0)
  //   Fig 2.1.3 De-Morgan's First Law(1,0)
  //   Fig 2.1.2 De-Morgan's First Law(0,1)
  //   Fig 2.1.4 De-Morgan's First Law(1,1)
endmodule
